# Fritzing sketch Etch-a-Sketch (saved by Fritzing 0.9.3b)
circuit board: 8.46667cm x 6cm
breadboards: 1

parts:
  Switch = Toggle Switch [package=THT]
  Battery = LIPO-110mAh [package=lipo-110]
  Converter = PowerBoost 500 Charger
  ENCODER1 = Rotary Encoder with Knob
  ENCODER2 = Rotary Encoder with Knob
  Screen = 3.5in TFT 480x320 Touch + MicroSD
  Arduino_Mini = Arduino Pro Mini v13

nets:
  N1: Switch.COM, Screen.+5V, Arduino_Mini.RAW
  N2: Battery.+, Converter.VBAT_IN
  N3: Battery.-, Converter.GND_BAT_IN
  GND: Converter.GND, ENCODER1.no_name_yet#2, ENCODER1.no_name_yet#5, ENCODER2.no_name_yet#2, ENCODER2.no_name_yet#5, Screen.GND, Arduino_Mini.GND
  N4: ENCODER1.no_name_yet#1, Arduino_Mini.D6_PWM
  N5: ENCODER1.no_name_yet#3, Arduino_Mini.D5_PWM
  N6: ENCODER1.no_name_yet#4, Arduino_Mini.D7
  N7: ENCODER2.no_name_yet#1, Arduino_Mini.D3_PWM
  N8: ENCODER2.no_name_yet#3, Arduino_Mini.D2
  N9: ENCODER2.no_name_yet#4, Arduino_Mini.D8
  N10: Screen.LCD_WR_5V, Arduino_Mini.D13/SCK
  N11: Screen.MISO, Arduino_Mini.D12/MISO
  N12: Screen.MOSI, Arduino_Mini.D11_PWM/MOSI
  N13: Screen.LCD_CS_5V, Arduino_Mini.D10_PWM/SS
  N14: Screen.LCD_RS_5V, Arduino_Mini.D9_PWM
  N15: Screen.Card_CS, Arduino_Mini.D4

custom parts:
  Rotary Encoder with Knob: Rotary Encoder with 1/4" Shaft and Knob
  3.5in TFT 480x320 Touch + MicroSD: This TFT display is big (3.5" diagonal), bright (6 white-LED backlight) and colorful! 480x320 pixels with individual RGB pixel control. This display also has a resistive touchscreen attached to it already, so you can detect finger presses anywhere on the screen. There is a controller built into the display with RAM buffering, so that almost no work is done by the microcontroller. The display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
