# Fritzing sketch etch-a-sketchpcb2 (saved by Fritzing 0.9.3b)
circuit board: 7.6cm x 3.85cm
breadboards: 1

parts:
  io = Toggle Switch [package=THT]
  P = female pin header, 2 pins [form="♀ (female)"]
  J4 = female pin header, 20 pins [form="♀ (female)"]
  Mini = Arduino Pro Mini v13
  R1 = female pin header, 5 pins [form="♀ (female)"]
  R1_2 = female pin header, 5 pins [form="♀ (female)"]

nets:
  N1: io.L1, P.pin2
  N2: io.COM, io.L2, J4.pin19, Mini.GND, R1.pin5, R1_2.pin1
  N3: P.pin1, J4.pin20, Mini.RAW
  N4: J4.pin2, Mini.D4
  N5: J4.pin14, Mini.D9_PWM
  N6: J4.pin15, Mini.D10_PWM/SS
  N7: J4.pin16, Mini.D11_PWM/MOSI
  N8: J4.pin17, Mini.D12/MISO
  N9: J4.pin18, Mini.D13/SCK
  N10: Mini.VCC, R1.pin4, R1_2.pin2
  N11: Mini.D8, R1.pin3
  N12: Mini.D7, R1.pin2
  N13: Mini.D6_PWM, R1.pin1
  N14: Mini.D5_PWM, R1_2.pin3
  N15: Mini.D3_PWM, R1_2.pin4
  N16: Mini.D2, R1_2.pin5
